# Fritzing sketch RadioMarellino3 (saved by Fritzing 1.0.7)
circuit board: 10.1116cm x 8.18652cm
breadboards: 1

parts:
  ESP32-S3 = ESP32-S2-DevKitC-1 [part_number=ESP32-S2-DevKitC-1]
  Right = Adafruit MAX98357A I2S 3W Class D Amplifier [part_number="Adafruit #3006"]
  +5V = DD4012SA [package=THT]
  Volume = KY-040 Rotary encoder [package="Breakout board"]
  +_Vin = screw terminal, 2 pins
  R1 = Resistor [tolerance=±5% power=0.25W resistance=220 package=THT]
  R2 = Resistor [tolerance=±5% power=0.25W resistance=220 package=THT]
  R3 = Resistor [tolerance=±5% power=0.25W resistance=220 package=THT]
  Left = Adafruit MAX98357A I2S 3W Class D Amplifier [part_number="Adafruit #3006"]
  Sinto = KY-040 Rotary encoder [package="Breakout board"]
  A1 = ESP32-S3-WROOM-1-N16R8 dev board
  C2 = Capacitor Polarized [package=cpol-radial-100uf-25v]
  C1 = Capacitor Polarized [package=cpol-radial-100uf-25v]

nets:
  VCC: ESP32-S3.pin_1, ESP32-S3.pin_2, Volume.Vcc, Sinto.Vcc, A1.Pin_1, A1.Pin_2
  N1: ESP32-S3.pin_3, A1.Pin_3
  N2: ESP32-S3.pin_4, Sinto.DT, A1.Pin_4
  N3: ESP32-S3.pin_5, Sinto.CLK, A1.Pin_5
  N4: ESP32-S3.pin_6, A1.Pin_6
  N5: ESP32-S3.pin_7, A1.Pin_7
  N6: ESP32-S3.pin_8, A1.Pin_8
  N7: ESP32-S3.pin_9, A1.Pin_9
  N8: ESP32-S3.pin_10, A1.Pin_10
  N9: ESP32-S3.pin_11, A1.Pin_11
  N10: ESP32-S3.pin_12, A1.Pin_12
  N11: ESP32-S3.pin_13, A1.Pin_13
  N12: ESP32-S3.pin_14, A1.Pin_14
  N13: ESP32-S3.pin_15, Volume.SW, A1.Pin_15
  N14: ESP32-S3.pin_16, Sinto.SW, A1.Pin_16
  N15: ESP32-S3.pin_17, A1.Pin_17
  N16: ESP32-S3.pin_18, Right.DIN, Left.DIN, A1.Pin_18
  N17: ESP32-S3.pin_19, Right.BCLK, R3.Pin_0, Left.BCLK, A1.Pin_19
  N18: ESP32-S3.pin_20, Right.LRCLK, Left.LRCLK, A1.Pin_20
  VIN: ESP32-S3.pin_21, Right.VIN, +5V.pin3, Left.VIN, A1.Pin_21, C2.+, C1.+
  GND: ESP32-S3.pin_22, ESP32-S3.pin_23, ESP32-S3.pin_24, ESP32-S3.pin_44, +5V.pin2, Volume.GND, +_Vin.pin2, Sinto.GND, A1.Pin_22, A1.Pin_23, A1.Pin_24, A1.Pin_44
  N19: ESP32-S3.pin_25, A1.Pin_25
  N20: ESP32-S3.pin_26, A1.Pin_26
  N21: ESP32-S3.pin_27, A1.Pin_27
  N22: ESP32-S3.pin_28, A1.Pin_28
  N23: ESP32-S3.pin_29, A1.Pin_29
  N24: ESP32-S3.pin_30, A1.Pin_30
  N25: ESP32-S3.pin_31, A1.Pin_31
  N26: ESP32-S3.pin_32, A1.Pin_32
  N27: ESP32-S3.pin_33, A1.Pin_33
  N28: ESP32-S3.pin_34, A1.Pin_34
  N29: ESP32-S3.pin_35, A1.Pin_35
  N30: ESP32-S3.pin_36, A1.Pin_36
  N31: ESP32-S3.pin_37, A1.Pin_37
  N32: ESP32-S3.pin_38, Volume.CLK, A1.Pin_38
  N33: ESP32-S3.pin_39, Volume.DT, A1.Pin_39
  N34: ESP32-S3.pin_40, A1.Pin_40
  N35: ESP32-S3.pin_41, A1.Pin_41
  N36: ESP32-S3.pin_42, A1.Pin_42
  N37: ESP32-S3.pin_43, A1.Pin_43
  N38: Right.GND, C1.-
  N39: Right.SD_MODE, R1.Pin_0
  N40: +5V.pin1, +_Vin.pin1
  N41: R1.Pin_1, R2.Pin_1, R3.Pin_1
  N42: R2.Pin_0, Left.SD_MODE
  N43: Left.GND, C2.-

custom parts:
  ESP32-S2-DevKitC-1: ESP32-S2-DevKitC-1 is an entry-level development board based on ESP32-S2-SOLO (on-board PCB antenna). It is based on the ESP32 microcontroller that boasts Wifi, Bluetooth, Ethernet and Low Power support all in a single chip. (vanepp) Feb 2022: converted to ESP32-S2-DevKitC-1. This module is 44pins long (2x22) and 11 pins width.
  Adafruit MAX98357A I2S 3W Class D Amplifier: Listen to this good news - we now have an all in one digital audio amp breakout board that works incredibly well with the Raspberry Pi! If you're looking for an easy and low cost way to get you digital sound files bumpin' then the MAX08357 I2S Amp Breakout is for you. It takes standard I2S digital audio input and, not only decodes it into analog, but also amplifies it directly into a speaker.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
  DD4012SA: DD4012SA 1A DC 5V 6V 9V 12V 24V to 3.3V 5V DC-DC Step-Down Buck Converter Regulator Module Board.
  KY-040 Rotary encoder: KY-040 Rotary Encoder with switch on breakout borad from AZ Delivery
  ESP32-S3-WROOM-1-N16R8 dev board: ESP32-S3 WIFI+BLE5.0 Development Board ESP32-S3-WROOM-1-N16R8(16M Flash/8SRAM).
