# Fritzing sketch RadioMarellino4 (saved by Fritzing 1.0.8)
circuit board: 9.8413cm x 8.33575cm
breadboards: 1

parts:
  Right = Adafruit MAX98357A I2S 3W Class D Amplifier [part_number="Adafruit #3006"]
  +5V = DD4012SA [package=THT]
  Volume = KY-040 Rotary encoder [package="Breakout board"]
  +_Vin = screw terminal, 2 pins
  R1 = Resistor [tolerance=±5% power=0.25W resistance=220 package=THT]
  R2 = Resistor [tolerance=±5% power=0.25W resistance=220 package=THT]
  R3 = Resistor [tolerance=±5% power=0.25W resistance=220 package=THT]
  Left = Adafruit MAX98357A I2S 3W Class D Amplifier [part_number="Adafruit #3006"]
  Sinto = KY-040 Rotary encoder [package="Breakout board"]
  A1 = ESP32-S3-WROOM-1-N16R8 dev board
  C2 = Capacitor Polarized [package=cpol-radial-100uf-25v]
  C1 = Capacitor Polarized [package=cpol-radial-100uf-25v]
  ESP32-S3 = ESP32-S2-DevKitC-1 [part_number=ESP32-S2-DevKitC-1]
  A2 = ESP32 DevKitc V4  # not connected

nets:
  VIN: Right.VIN, +5V.pin3, Left.VIN, A1.Pin_21, C2.+, C1.+, ESP32-S3.pin_21
  GND: Right.GND, +5V.pin2, Volume.GND, +_Vin.pin2, Left.GND, Sinto.GND, A1.Pin_22, A1.Pin_23, A1.Pin_24, A1.Pin_44, C2.-, C1.-, ESP32-S3.pin_22, ESP32-S3.pin_23, ESP32-S3.pin_24, ESP32-S3.pin_44
  N1: Right.SD_MODE, R1.Pin_0
  N2: Right.DIN, Left.DIN, A1.Pin_18, ESP32-S3.pin_18
  N3: Right.BCLK, R3.Pin_0, Left.BCLK, A1.Pin_19, ESP32-S3.pin_19
  N4: Right.LRCLK, Left.LRCLK, A1.Pin_20, ESP32-S3.pin_20
  N5: +5V.pin1, +_Vin.pin1
  VCC: Volume.Vcc, R1.Pin_1, R2.Pin_1, R3.Pin_1, Sinto.Vcc, A1.Pin_1, A1.Pin_2, ESP32-S3.pin_1, ESP32-S3.pin_2
  N6: Volume.SW, A1.Pin_15, ESP32-S3.pin_15
  N7: Volume.DT, A1.Pin_39, ESP32-S3.pin_39
  N8: Volume.CLK, A1.Pin_38, ESP32-S3.pin_38
  N9: R2.Pin_0, Left.SD_MODE
  N10: Sinto.SW, A1.Pin_16, ESP32-S3.pin_16
  N11: Sinto.DT, A1.Pin_4, ESP32-S3.pin_4
  N12: Sinto.CLK, A1.Pin_5, ESP32-S3.pin_5
  N13: A1.Pin_3, ESP32-S3.pin_3
  N14: A1.Pin_6, ESP32-S3.pin_6
  N15: A1.Pin_7, ESP32-S3.pin_7
  N16: A1.Pin_8, ESP32-S3.pin_8
  N17: A1.Pin_9, ESP32-S3.pin_9
  N18: A1.Pin_10, ESP32-S3.pin_10
  N19: A1.Pin_11, ESP32-S3.pin_11
  N20: A1.Pin_12, ESP32-S3.pin_12
  N21: A1.Pin_13, ESP32-S3.pin_13
  N22: A1.Pin_14, ESP32-S3.pin_14
  N23: A1.Pin_17, ESP32-S3.pin_17
  N24: A1.Pin_25, ESP32-S3.pin_25
  N25: A1.Pin_26, ESP32-S3.pin_26
  N26: A1.Pin_27, ESP32-S3.pin_27
  N27: A1.Pin_28, ESP32-S3.pin_28
  N28: A1.Pin_29, ESP32-S3.pin_29
  N29: A1.Pin_30, ESP32-S3.pin_30
  N30: A1.Pin_31, ESP32-S3.pin_31
  N31: A1.Pin_32, ESP32-S3.pin_32
  N32: A1.Pin_33, ESP32-S3.pin_33
  N33: A1.Pin_34, ESP32-S3.pin_34
  N34: A1.Pin_35, ESP32-S3.pin_35
  N35: A1.Pin_36, ESP32-S3.pin_36
  N36: A1.Pin_37, ESP32-S3.pin_37
  N37: A1.Pin_40, ESP32-S3.pin_40
  N38: A1.Pin_41, ESP32-S3.pin_41
  N39: A1.Pin_42, ESP32-S3.pin_42
  N40: A1.Pin_43, ESP32-S3.pin_43

custom parts:
  Adafruit MAX98357A I2S 3W Class D Amplifier: Listen to this good news - we now have an all in one digital audio amp breakout board that works incredibly well with the Raspberry Pi! If you're looking for an easy and low cost way to get you digital sound files bumpin' then the MAX08357 I2S Amp Breakout is for you. It takes standard I2S digital audio input and, not only decodes it into analog, but also amplifies it directly into a speaker.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
  DD4012SA: DD4012SA 1A DC 5V 6V 9V 12V 24V to 3.3V 5V DC-DC Step-Down Buck Converter Regulator Module Board.
  KY-040 Rotary encoder: KY-040 Rotary Encoder with switch on breakout borad from AZ Delivery
  ESP32-S3-WROOM-1-N16R8 dev board: ESP32-S3 WIFI+BLE5.0 Development Board ESP32-S3-WROOM-1-N16R8(16M Flash/8SRAM).
  ESP32-S2-DevKitC-1: ESP32-S2-DevKitC-1 is an entry-level development board based on ESP32-S2-SOLO (on-board PCB antenna). It is based on the ESP32 microcontroller that boasts Wifi, Bluetooth, Ethernet and Low Power support all in a single chip. (vanepp) Feb 2022: converted to ESP32-S2-DevKitC-1. This module is 44pins long (2x22) and 11 pins width.
  ESP32 DevKitc V4: ESP32-DevKitC board with ESP32-WROOM-32 module. ESP32-DevKitC V4 is a small-sized ESP32-based development board produced by Espressif. Most of the pins on the ESP module are broken out to the pin headers on the board. The pins D0, D1, D2, D3, CMD and CLK are used internally for communication between ESP32 and SPI flash memory. They are grouped on both sides near the USB connector. Avoid using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
